// Logisim project miicroprocesseur-16bits.circ as structural Verilog: 6 circuits, main circuit main
module main (
  input  [3:0] in_1,
  input  [15:0] in_2,
  input  in_3,
  input  [3:0] in_4,
  input  in_5,
  input  in_6,
  output [15:0] out_7,
  output [3:0] out_8,
  output [15:0] out_9,
  output [2:0] out_10,
  output out_11,
  output [15:0] out_12,
  output [3:0] out_13,
  output [2:0] OP
);

  wire button_1_out, clock_1_out, clock_2_out, clock_3_out, comparator_1_eq, not_1_out, pull_resistor_1_node;
  wire [11:0] ram_1_data;
  wire [15:0] adder_1_out, multiplexer_1_out, register_1_q;

  Adder #(.width(16)) adder_1 (.a(register_1_q), .b(16'h1), .out(adder_1_out));  // open: cin, cout
  not not_1 (not_1_out, comparator_1_eq);
  Comparator #(.width(16)) comparator_1 (.a(register_1_q), .b(16'h1111), .eq(comparator_1_eq));  // open: gt, lt
  Register #(.width(16), .trigger("falling")) register_1 (
    .D(adder_1_out), .en(not_1_out), .Q(register_1_q), .clk(clock_1_out), .clr(button_1_out));
  Clock clock_1 (.out(clock_1_out));
  Button button_1 (.out(button_1_out));
  Pull_Resistor #(.pull(1)) pull_resistor_1 (.node(pull_resistor_1_node));
  Clock clock_2 (.out(clock_2_out));
  RAM #(.addrWidth(16), .dataWidth(16), .bus("separate")) ram_1 (
    .addr(register_1_q), .data({out_11, OP, ram_1_data}), .clk(clock_2_out), .ld(pull_resistor_1_node),
    .clr(in_6));  // open: din, str, sel
  Multiplexer #(.width(16)) multiplexer_1 (.in0(out_9), .in1(in_2), .out(multiplexer_1_out), .sel(in_3));  // open: en
  Multiplexer #(.width(4)) multiplexer_2 (.in0(in_4), .in1(ram_1_data[3:0]), .out(out_8), .sel(in_5));  // open: en
  rf16 rf16_1 (
    .WD3(multiplexer_1_out), .A1(out_8), .A2(ram_1_data[11:8]), .A3(ram_1_data[7:4]), .rd1(out_7),
    .RD2(out_12), .clk(clock_3_out));
  Clock clock_3 (.out(clock_3_out));
  alu16bits alu16bits_1 (
    .in_1(out_7), .in_2(out_12), .re_plus(in_1[3]), .rs_plus(out_13[3]), .re_minus(in_1[2]),
    .rs_minus(out_13[2]), .re_star(in_1[1]), .rs_star(out_13[1]), .re(in_1[0]), .rs(out_13[0]), .in_7(OP),
    .out_12(out_10), .out_13(out_9));

  // Notes on the sheet:
  //   PC
  //   0000  0000 0000
  //   Registre file
  //   A
  //   B
  //   001 ->Sub
  //   010 ->MUL
  //   011 ->Div
  //   ALU
  //   100 ->AND
  //   101 ->OR
  //   110 ->NOR
  //   111 ->Inverse
  //   ALU
  //   000 -> add
  //   Resultat
endmodule

module alu1bits (
  input  A,
  input  B,
  input  RE_plus,
  input  RE_minus,
  input  RE_star,
  input  RE,
  input  [2:0] in_7,
  output out_8,
  output out_9,
  output out_10,
  output out_11,
  output [2:0] out_12,
  output S
);

  wire add_s, and_1_out, divider_1_out, multiplier_1_out, nor_1_out, not_1_out, or_1_out, subtractor_1_out;

  add add (.A(A), .B(B), .re(RE_plus), .RS(out_8), .S(add_s));
  Subtractor #(.width(1)) subtractor_1 (.a(A), .b(B), .out(subtractor_1_out), .bin(RE_minus), .bout(out_9));
  Multiplier #(.width(1)) multiplier_1 (.a(A), .b(B), .out(multiplier_1_out), .cin(RE_star), .cout(out_10));
  Divider #(.width(1)) divider_1 (.a(A), .b(B), .out(divider_1_out), .upper(RE), .rem(out_11));
  and and_1 (and_1_out, A, B);
  or or_1 (or_1_out, A, B);
  nor nor_1 (nor_1_out, A, B);
  not not_1 (not_1_out, A);
  Multiplexer #(.select(3)) multiplexer_1 (
    .in0(add_s), .in1(subtractor_1_out), .in2(multiplier_1_out), .in3(divider_1_out), .in4(and_1_out),
    .in5(or_1_out), .in6(nor_1_out), .in7(not_1_out), .out(S), .sel(in_7));  // open: en
  sub sub_1 ();  // open: A, B, re, RS, S

  assign out_12 = in_7;

  // Notes on the sheet:
  //   sub
endmodule

module add (
  input  A,
  input  B,
  input  re,
  output RS,
  output S
);

  wire and_1_out, and_2_out, or_1_out, xor_1_out;

  and and_1 (and_1_out, A, B);
  or or_1 (or_1_out, A, B);
  and and_2 (and_2_out, or_1_out, re);
  xor xor_1 (xor_1_out, A, B);
  or or_2 (RS, and_1_out, and_2_out);
  xor xor_2 (S, xor_1_out, re);
endmodule

module sub (
  input  A,
  input  B,
  input  re,
  output RS,
  output S
);

  wire and_1_out, and_2_out, not_1_out, or_1_out, xor_1_out;

  not not_1 (not_1_out, B);
  and and_1 (and_1_out, A, not_1_out);
  or or_1 (or_1_out, A, not_1_out);
  and and_2 (and_2_out, or_1_out, re);
  xor xor_1 (xor_1_out, A, not_1_out);
  or or_2 (RS, and_1_out, and_2_out);
  xor xor_2 (S, xor_1_out, re);
endmodule

module alu16bits (
  input  [15:0] in_1,
  input  [15:0] in_2,
  input  re_plus,
  input  re_minus,
  input  re_star,
  input  re,
  input  [2:0] in_7,
  output rs_plus,
  output rs_minus,
  output rs_star,
  output rs,
  output [2:0] out_12,
  output [15:0] out_13
);

  wire alu1bits_1_out_8, alu1bits_1_out_9, alu1bits_1_out_10, alu1bits_1_out_11, alu1bits_2_out_8,
       alu1bits_2_out_9, alu1bits_2_out_10, alu1bits_2_out_11, alu1bits_3_out_8, alu1bits_3_out_9,
       alu1bits_3_out_10, alu1bits_3_out_11, alu1bits_4_out_8, alu1bits_4_out_9, alu1bits_4_out_10,
       alu1bits_4_out_11, alu1bits_5_out_8, alu1bits_5_out_9, alu1bits_5_out_10, alu1bits_5_out_11,
       alu1bits_6_out_8, alu1bits_6_out_9, alu1bits_6_out_10, alu1bits_6_out_11, alu1bits_7_out_8,
       alu1bits_7_out_9, alu1bits_7_out_10, alu1bits_7_out_11, alu1bits_8_out_8, alu1bits_8_out_9,
       alu1bits_8_out_10, alu1bits_8_out_11, alu1bits_9_out_8, alu1bits_9_out_9, alu1bits_9_out_10,
       alu1bits_9_out_11, alu1bits_10_out_8, alu1bits_10_out_9, alu1bits_10_out_10, alu1bits_10_out_11,
       alu1bits_11_out_8, alu1bits_11_out_9, alu1bits_11_out_10, alu1bits_11_out_11, alu1bits_12_out_8,
       alu1bits_12_out_9, alu1bits_12_out_10, alu1bits_12_out_11, alu1bits_13_out_8, alu1bits_13_out_9,
       alu1bits_13_out_10, alu1bits_13_out_11, alu1bits_14_out_8, alu1bits_14_out_9, alu1bits_14_out_10,
       alu1bits_14_out_11, alu1bits_15_out_8, alu1bits_15_out_9, alu1bits_15_out_10, alu1bits_15_out_11;
  wire [2:0] alu1bits_1_out_12, alu1bits_2_out_12, alu1bits_3_out_12, alu1bits_4_out_12, alu1bits_5_out_12,
       alu1bits_6_out_12, alu1bits_7_out_12, alu1bits_8_out_12, alu1bits_9_out_12, alu1bits_10_out_12,
       alu1bits_11_out_12, alu1bits_12_out_12, alu1bits_13_out_12, alu1bits_14_out_12, alu1bits_15_out_12;

  alu1bits alu1bits_1 (
    .RE_plus(re_plus), .RE_minus(re_minus), .RE_star(re_star), .RE(re), .in_7(in_7), .A(in_1[0]),
    .B(in_2[0]), .out_8(alu1bits_1_out_8), .out_9(alu1bits_1_out_9), .out_10(alu1bits_1_out_10),
    .out_11(alu1bits_1_out_11), .out_12(alu1bits_1_out_12), .S(out_13[0]));
  alu1bits alu1bits_2 (
    .RE_plus(alu1bits_1_out_8), .RE_minus(alu1bits_1_out_9), .RE_star(alu1bits_1_out_10),
    .RE(alu1bits_1_out_11), .in_7(alu1bits_1_out_12), .A(in_1[1]), .B(in_2[1]), .out_8(alu1bits_2_out_8),
    .out_9(alu1bits_2_out_9), .out_10(alu1bits_2_out_10), .out_11(alu1bits_2_out_11),
    .out_12(alu1bits_2_out_12), .S(out_13[1]));
  alu1bits alu1bits_3 (
    .RE_plus(alu1bits_2_out_8), .RE_minus(alu1bits_2_out_9), .RE_star(alu1bits_2_out_10),
    .RE(alu1bits_2_out_11), .in_7(alu1bits_2_out_12), .A(in_1[2]), .B(in_2[2]), .out_8(alu1bits_3_out_8),
    .out_9(alu1bits_3_out_9), .out_10(alu1bits_3_out_10), .out_11(alu1bits_3_out_11),
    .out_12(alu1bits_3_out_12), .S(out_13[2]));
  alu1bits alu1bits_4 (
    .RE_plus(alu1bits_3_out_8), .RE_minus(alu1bits_3_out_9), .RE_star(alu1bits_3_out_10),
    .RE(alu1bits_3_out_11), .in_7(alu1bits_3_out_12), .A(in_1[3]), .B(in_2[3]), .out_8(alu1bits_4_out_8),
    .out_9(alu1bits_4_out_9), .out_10(alu1bits_4_out_10), .out_11(alu1bits_4_out_11),
    .out_12(alu1bits_4_out_12), .S(out_13[3]));
  alu1bits alu1bits_5 (
    .RE_plus(alu1bits_4_out_8), .RE_minus(alu1bits_4_out_9), .RE_star(alu1bits_4_out_10),
    .RE(alu1bits_4_out_11), .in_7(alu1bits_4_out_12), .A(in_1[4]), .B(in_2[4]), .out_8(alu1bits_5_out_8),
    .out_9(alu1bits_5_out_9), .out_10(alu1bits_5_out_10), .out_11(alu1bits_5_out_11),
    .out_12(alu1bits_5_out_12), .S(out_13[4]));
  alu1bits alu1bits_6 (
    .RE_plus(alu1bits_7_out_8), .RE_minus(alu1bits_7_out_9), .RE_star(alu1bits_7_out_10),
    .RE(alu1bits_7_out_11), .in_7(alu1bits_7_out_12), .A(in_1[6]), .B(in_2[6]), .out_8(alu1bits_6_out_8),
    .out_9(alu1bits_6_out_9), .out_10(alu1bits_6_out_10), .out_11(alu1bits_6_out_11),
    .out_12(alu1bits_6_out_12), .S(out_13[6]));
  alu1bits alu1bits_7 (
    .RE_plus(alu1bits_5_out_8), .RE_minus(alu1bits_5_out_9), .RE_star(alu1bits_5_out_10),
    .RE(alu1bits_5_out_11), .in_7(alu1bits_5_out_12), .A(in_1[5]), .B(in_2[5]), .out_8(alu1bits_7_out_8),
    .out_9(alu1bits_7_out_9), .out_10(alu1bits_7_out_10), .out_11(alu1bits_7_out_11),
    .out_12(alu1bits_7_out_12), .S(out_13[5]));
  alu1bits alu1bits_8 (
    .RE_plus(alu1bits_6_out_8), .RE_minus(alu1bits_6_out_9), .RE_star(alu1bits_6_out_10),
    .RE(alu1bits_6_out_11), .in_7(alu1bits_6_out_12), .A(in_1[7]), .B(in_2[7]), .out_8(alu1bits_8_out_8),
    .out_9(alu1bits_8_out_9), .out_10(alu1bits_8_out_10), .out_11(alu1bits_8_out_11),
    .out_12(alu1bits_8_out_12), .S(out_13[7]));
  alu1bits alu1bits_9 (
    .RE_plus(alu1bits_8_out_8), .RE_minus(alu1bits_8_out_9), .RE_star(alu1bits_8_out_10),
    .RE(alu1bits_8_out_11), .in_7(alu1bits_8_out_12), .A(in_1[8]), .B(in_2[8]), .out_8(alu1bits_9_out_8),
    .out_9(alu1bits_9_out_9), .out_10(alu1bits_9_out_10), .out_11(alu1bits_9_out_11),
    .out_12(alu1bits_9_out_12), .S(out_13[8]));
  alu1bits alu1bits_10 (
    .RE_plus(alu1bits_9_out_8), .RE_minus(alu1bits_9_out_9), .RE_star(alu1bits_9_out_10),
    .RE(alu1bits_9_out_11), .in_7(alu1bits_9_out_12), .A(in_1[9]), .B(in_2[9]), .out_8(alu1bits_10_out_8),
    .out_9(alu1bits_10_out_9), .out_10(alu1bits_10_out_10), .out_11(alu1bits_10_out_11),
    .out_12(alu1bits_10_out_12), .S(out_13[9]));
  alu1bits alu1bits_11 (
    .RE_plus(alu1bits_10_out_8), .RE_minus(alu1bits_10_out_9), .RE_star(alu1bits_10_out_10),
    .RE(alu1bits_10_out_11), .in_7(alu1bits_10_out_12), .A(in_1[10]), .B(in_2[10]),
    .out_8(alu1bits_11_out_8), .out_9(alu1bits_11_out_9), .out_10(alu1bits_11_out_10),
    .out_11(alu1bits_11_out_11), .out_12(alu1bits_11_out_12), .S(out_13[10]));
  alu1bits alu1bits_12 (
    .RE_plus(alu1bits_11_out_8), .RE_minus(alu1bits_11_out_9), .RE_star(alu1bits_11_out_10),
    .RE(alu1bits_11_out_11), .in_7(alu1bits_11_out_12), .A(in_1[11]), .B(in_2[11]),
    .out_8(alu1bits_12_out_8), .out_9(alu1bits_12_out_9), .out_10(alu1bits_12_out_10),
    .out_11(alu1bits_12_out_11), .out_12(alu1bits_12_out_12), .S(out_13[11]));
  alu1bits alu1bits_13 (
    .RE_plus(alu1bits_12_out_8), .RE_minus(alu1bits_12_out_9), .RE_star(alu1bits_12_out_10),
    .RE(alu1bits_12_out_11), .in_7(alu1bits_12_out_12), .A(in_1[12]), .B(in_2[12]),
    .out_8(alu1bits_13_out_8), .out_9(alu1bits_13_out_9), .out_10(alu1bits_13_out_10),
    .out_11(alu1bits_13_out_11), .out_12(alu1bits_13_out_12), .S(out_13[12]));
  alu1bits alu1bits_14 (
    .RE_plus(alu1bits_13_out_8), .RE_minus(alu1bits_13_out_9), .RE_star(alu1bits_13_out_10),
    .RE(alu1bits_13_out_11), .in_7(alu1bits_13_out_12), .A(in_1[13]), .B(in_2[13]),
    .out_8(alu1bits_14_out_8), .out_9(alu1bits_14_out_9), .out_10(alu1bits_14_out_10),
    .out_11(alu1bits_14_out_11), .out_12(alu1bits_14_out_12), .S(out_13[13]));
  alu1bits alu1bits_15 (
    .RE_plus(alu1bits_14_out_8), .RE_minus(alu1bits_14_out_9), .RE_star(alu1bits_14_out_10),
    .RE(alu1bits_14_out_11), .in_7(alu1bits_14_out_12), .A(in_1[14]), .B(in_2[14]),
    .out_8(alu1bits_15_out_8), .out_9(alu1bits_15_out_9), .out_10(alu1bits_15_out_10),
    .out_11(alu1bits_15_out_11), .out_12(alu1bits_15_out_12), .S(out_13[14]));
  alu1bits alu1bits_16 (
    .RE_plus(alu1bits_15_out_8), .RE_minus(alu1bits_15_out_9), .RE_star(alu1bits_15_out_10),
    .RE(alu1bits_15_out_11), .in_7(alu1bits_15_out_12), .A(in_1[15]), .B(in_2[15]), .out_8(rs_plus),
    .out_9(rs_minus), .out_10(rs_star), .out_11(rs), .out_12(out_12), .S(out_13[15]));

  // Notes on the sheet:
  //   A
  //   B
  //   S
endmodule

module rf16 (
  input  clk,
  input  [15:0] WD3,
  input  [3:0] A1,
  input  [3:0] A2,
  input  [3:0] A3,
  output [15:0] rd1,
  output [15:0] RD2
);

  wire and_1_out, and_2_out, and_3_out, and_4_out, and_5_out, and_6_out, and_7_out, and_8_out, and_9_out,
       and_10_out, and_11_out, and_12_out, and_13_out, and_14_out, and_15_out, and_16_out, decoder_1_out0,
       decoder_1_out1, decoder_1_out2, decoder_1_out3, decoder_1_out4, decoder_1_out5, decoder_1_out6,
       decoder_1_out7, decoder_1_out8, decoder_1_out9, decoder_1_out10, decoder_1_out11, decoder_1_out12,
       decoder_1_out13, decoder_1_out14, decoder_1_out15;
  wire [15:0] register_1_q, register_2_q, register_3_q, register_4_q, register_5_q, register_6_q,
       register_7_q, register_8_q, register_9_q, register_10_q, register_11_q, register_12_q, register_13_q,
       register_14_q, register_15_q, register_16_q;

  Decoder #(.select(4)) decoder_1 (
    .out0(decoder_1_out0), .out1(decoder_1_out1), .out2(decoder_1_out2), .out3(decoder_1_out3),
    .out4(decoder_1_out4), .out5(decoder_1_out5), .out6(decoder_1_out6), .out7(decoder_1_out7),
    .out8(decoder_1_out8), .out9(decoder_1_out9), .out10(decoder_1_out10), .out11(decoder_1_out11),
    .out12(decoder_1_out12), .out13(decoder_1_out13), .out14(decoder_1_out14), .out15(decoder_1_out15),
    .sel(A1));  // open: en
  and and_1 (and_1_out, decoder_1_out0, clk);
  and and_2 (and_2_out, decoder_1_out1, clk);
  and and_3 (and_3_out, decoder_1_out2, clk);
  and and_4 (and_4_out, decoder_1_out3, clk);
  and and_5 (and_5_out, decoder_1_out4, clk);
  and and_6 (and_6_out, decoder_1_out5, clk);
  and and_7 (and_7_out, decoder_1_out6, clk);
  and and_8 (and_8_out, decoder_1_out7, clk);
  and and_9 (and_9_out, decoder_1_out8, clk);
  and and_10 (and_10_out, decoder_1_out9, clk);
  and and_11 (and_11_out, decoder_1_out10, clk);
  and and_12 (and_12_out, decoder_1_out11, clk);
  and and_13 (and_13_out, decoder_1_out12, clk);
  and and_14 (and_14_out, decoder_1_out13, clk);
  and and_15 (and_15_out, decoder_1_out14, clk);
  and and_16 (and_16_out, decoder_1_out15, clk);
  Register #(.width(16)) register_1 (.D(WD3), .Q(register_1_q), .clk(and_1_out));  // open: en, clr
  Register #(.width(16)) register_2 (.D(WD3), .Q(register_2_q), .clk(and_2_out));  // open: en, clr
  Register #(.width(16)) register_3 (.D(WD3), .Q(register_3_q), .clk(and_3_out));  // open: en, clr
  Register #(.width(16)) register_4 (.D(WD3), .Q(register_4_q), .clk(and_4_out));  // open: en, clr
  Register #(.width(16)) register_5 (.D(WD3), .Q(register_5_q), .clk(and_5_out), .clr(and_5_out));  // open: en
  Register #(.width(16)) register_6 (.D(WD3), .Q(register_6_q), .clk(and_6_out));  // open: en, clr
  Register #(.width(16)) register_7 (.D(WD3), .Q(register_7_q), .clk(and_7_out));  // open: en, clr
  Register #(.width(16)) register_8 (.D(WD3), .Q(register_8_q), .clk(and_8_out));  // open: en, clr
  Register #(.width(16)) register_9 (.D(WD3), .Q(register_9_q), .clk(and_9_out));  // open: en, clr
  Register #(.width(16)) register_10 (.D(WD3), .Q(register_10_q), .clk(and_10_out));  // open: en, clr
  Register #(.width(16)) register_11 (.D(WD3), .Q(register_11_q), .clk(and_11_out));  // open: en, clr
  Register #(.width(16)) register_12 (.D(WD3), .Q(register_12_q), .clk(and_12_out));  // open: en, clr
  Register #(.width(16)) register_13 (.D(WD3), .Q(register_13_q), .clk(and_13_out), .clr(and_13_out));  // open: en
  Register #(.width(16)) register_14 (.D(WD3), .Q(register_14_q), .clk(and_14_out));  // open: en, clr
  Register #(.width(16)) register_15 (.D(WD3), .Q(register_15_q), .clk(and_15_out));  // open: en, clr
  Register #(.width(16)) register_16 (.D(WD3), .Q(register_16_q), .clk(and_16_out));  // open: en, clr
  Multiplexer #(.select(4), .width(16)) multiplexer_1 (
    .in0(register_1_q), .in1(register_2_q), .in2(register_3_q), .in3(register_4_q), .in4(register_5_q),
    .in5(register_6_q), .in6(register_7_q), .in7(register_8_q), .in8(register_9_q), .in9(register_10_q),
    .in10(register_11_q), .in11(register_12_q), .in12(register_13_q), .in13(register_14_q),
    .in14(register_15_q), .in15(register_16_q), .out(rd1), .sel(A2));  // open: en
  Multiplexer #(.select(4), .width(16)) multiplexer_2 (
    .in0(register_1_q), .in1(register_2_q), .in2(register_3_q), .in3(register_4_q), .in4(register_5_q),
    .in5(register_6_q), .in6(register_7_q), .in7(register_8_q), .in8(register_9_q), .in9(register_10_q),
    .in10(register_11_q), .in11(register_12_q), .in12(register_13_q), .in13(register_14_q),
    .in14(register_15_q), .in15(register_16_q), .out(RD2), .sel(A3));  // open: en
endmodule
